# Fritzing sketch minigames (saved by Fritzing 1.0.6)
breadboards: 1

parts:
  Part1 = Adafruit ESP32 Feather V2
  LED1 = LED - 5mm [color="Red (633nm)" current=0.030A package="5 mm [THT]"]
  LED2 = LED - 5mm [color="Yellow (585nm)" current=0.030A package="5 mm [THT]"]
  LED3 = LED - 5mm [color="Green (555nm)" current=0.030A package="5 mm [THT]"]
  S1 = Pushbutton [package="[THT]"]
  S2 = Pushbutton [package="[THT]"]
  R1 = Resistor [tolerance=±5% power=0.25W resistance=220 package=THT]
  R2 = Resistor [tolerance=±5% power=0.25W resistance=220 package=THT]
  S3 = Pushbutton [package="[THT]"]
  R3 = Resistor [tolerance=±5% power=0.25W resistance=220 package=THT]
  Part2 = LCD1602-I2C
  R4 = TRIMPOT [maximum_resistance=10kΩ knob_status=50% power=0.5W package=3386u]

nets:
  GND: Part1.GND, R1.Pin_1, R2.Pin_1, R3.Pin_1, Part2.GND, R4.CW
  N1: Part1.SDA, Part1.IO27_A10, LED3.cathode, Part2.SDA
  N2: Part1.A2_I34, R4.WIPER
  3.3V: Part1.3.3V, Part2.VCC, R4.CCW
  N3: Part1.IO12_A11, LED1.cathode
  N4: Part1.IO33_A9, LED2.cathode
  N5: Part1.SCL, Part2.SCL
  N6: LED1.anode, S1.Pin_3, S1.Pin_4
  N7: LED2.anode, S3.Pin_3, S3.Pin_4
  N8: LED3.anode, S2.Pin_3, S2.Pin_4
  N9: S1.Pin_1, S1.Pin_2, R1.Pin_0
  N10: S2.Pin_1, S2.Pin_2, R2.Pin_0
  N11: S3.Pin_1, S3.Pin_2, R3.Pin_0

custom parts:
  LCD1602-I2C: A standard character display, usually with 2x16 characters. Comes in many colors with LCM1602 IIC attached.
